# Fritzing sketch Esquema  Control Accesos (saved by Fritzing 0.9.6b)
breadboards: 1

parts:
  Componente1 = RFID-RC522-v3
  Generic_4x4_button_keypad1 = Generic 4x4 Keypad
  Componente2 = LCD1602-I2C
  MOTOR1 = Adafruit Gear-Reduced Stepper Motor (small)  # not connected
  BREAKOUT1 = ULN2003A breakout board  # not connected
  Componente3 = Arduino Uno (Rev3)

nets:
  N1: Componente1.SDA, Componente3.D10_PWM/SS
  N2: Componente1.SCK, Componente3.D13/SCK
  N3: Componente1.MOSI, Componente3.D11_PWM/MOSI
  N4: Componente1.MISO, Componente3.D12/MISO
  GND: Componente1.GND, Componente2.GND
  N5: Componente1.RST, Componente3.D9_PWM
  3.3V: Componente1.3.3V, Componente3.3V3
  N6: Generic_4x4_button_keypad1.C4, Componente3.D4
  N7: Generic_4x4_button_keypad1.C3, Componente3.D3_PWM
  N8: Generic_4x4_button_keypad1.C2, Componente3.D2
  N9: Generic_4x4_button_keypad1.C1, Componente3.A0
  N10: Generic_4x4_button_keypad1.R1, Componente3.A1
  N11: Generic_4x4_button_keypad1.R2, Componente3.A2
  N12: Generic_4x4_button_keypad1.R3, Componente3.A3
  N13: Generic_4x4_button_keypad1.R4, Componente2.SDA, Componente3.A4/SDA
  VCC: Componente2.VCC, Componente3.5V
  N14: Componente2.SCL, Componente3.A5/SCL

custom parts:
  RFID-RC522-v3: A simple China made RFID-RC522 Reader (6x4 cm); do check the pin labels, as this is a MFRC522 based clone.
  Generic 4x4 Keypad: generic 4x4 keypad 4 rows of four 6 mm tact switches cheap and nasty but works
  LCD1602-I2C: A standard character display, usually with 2x16 characters. Comes in many colors with LCM1602 IIC attached.
  Adafruit Gear-Reduced Stepper Motor (small): Adafruit gear-reduction stepper motor (small)
  ULN2003A breakout board: ULN2003A 7-way Darlington Transistor Driver on breakoutboard
